# Fritzing sketch MagicWand (saved by Fritzing 0.9.2b)
breadboards: 1

parts:
  Part1 = Arduino Uno (Rev3)
  R1 = Resistor [tolerance=±5% resistance=220 package=THT]
  R2 = Resistor [tolerance=±5% resistance=220 package=THT]
  R3 = Resistor [tolerance=±5% resistance=220 package=THT]
  R4 = Resistor [tolerance=±5% resistance=220 package=THT]  # not connected
  LED1 = RGB LED - (4 legs) [package="5 mm [THT]"]
  T1 = LM35 Temperature Sensor [package="TO92 [THT]"]
  R6 = Photocell (LDR) [package=THT]

nets:
  N1: Part1.A0, R2.Pin_0, R6.pin_1
  N2: Part1.A1, T1.Vout
  N3: Part1.5V, LED1.common_anode, T1.+Vs, R6.pin_0
  GND: Part1.GND, R2.Pin_1, T1.GND
  N4: R1.Pin_1, LED1.red_cathode
  N5: R3.Pin_1, LED1.green_cathode
